// Logisim project LEB32.circ as structural Verilog: 1 circuit, main circuit main
module main (
);

  wire ALU_en, and_1_out, and_2_out, and_3_out, and_4_out, and_5_out, and_6_out, and_7_out, clock_1_out,
       clock_2_out, clock_3_out, clock_4_out, clock_5_out, clock_6_out, clock_7_out, clock_8_out,
       comparator_1_eq, comparator_2_eq, comparator_2_gt, comparator_2_lt, comparator_3_gt, comparator_3_lt,
       counter_3_carry, counter_4_carry, d_ff_1_q, d_ff_1_qn, d_ff_2_q, decoder_1_out0, decoder_1_out1,
       decoder_1_out2, decoder_1_out3, decoder_1_out4, decoder_1_out5, decoder_1_out6, decoder_1_out7,
       decoder_1_out8, decoder_1_out9, decoder_1_out10, decoder_1_out11, decoder_1_out12, decoder_1_out13,
       decoder_1_out14, decoder_1_out15, decoder_2_out0, decoder_2_out1, hlt, jmp, mem_or_data,
       multiplexer_5_out, not_1_out, not_2_out, not_3_out, not_4_out, not_5_out, not_6_out, or_1_out,
       or_2_out, or_3_out, or_4_out, or_5_out, pll, psh, pull_resistor_4_node, reg_str, rgb_video_1_p2,
       s_r_ff_1_q, s_r_ff_1_qn, screenEN, undriven, we;
  wire [2:0] bit_extender_2_out, bit_extender_6_out;
  wire [3:0] inst_and_data_q, RegR1, RegR2, RegW;
  wire [4:0] bit_extender_5_out;
  wire [6:0] keyboard_1_data;
  wire [7:0] bit_extender_8_out, bit_extender_9_out, counter_1_q, pull_resistor_2_node, register_2_q,
       register_3_q, rgb_video_1_p3, rgb_video_1_p4, rom_2_data;
  wire [12:0] counter_3_q;
  wire [15:0] bit_extender_7_out, DATA;
  wire [23:0] MEMORY_ADDR, register_4_q, rgb_video_1_p5;
  wire [31:0] A_q, adder_1_out, adder_2_out, addr, ALU_out, B_q, bit_extender_1_out, bit_extender_3_out,
       bit_extender_4_out, C_q, D_q, divider_1_out, E_q, F_q, G_q, H_q, I_q, J_q, jmp_a, K_q, L_q, M_q,
       MEMORY_OUT, multiplexer_1_out, multiplexer_3_out, multiplexer_4_out, multiplexer_9_out,
       multiplier_1_out, multiplier_2_out, N_q, O_q, P_q, R1, R2, ram_1_dout, rom_1_data, shifter_1_out,
       shifter_2_out, stk_out, subtractor_1_out;

  assign bit_extender_1_out = {{16{1'b0}}, DATA};  // Bit_Extender bit_extender_1
  Multiplexer #(.width(32)) multiplexer_1 (
    .in0(bit_extender_1_out), .in1(MEMORY_OUT), .out(multiplexer_1_out), .sel(mem_or_data));
  Decoder #(.select(4)) decoder_1 (
    .out0(decoder_1_out0), .out1(decoder_1_out1), .out2(decoder_1_out2), .out3(decoder_1_out3),
    .out4(decoder_1_out4), .out5(decoder_1_out5), .out6(decoder_1_out6), .out7(decoder_1_out7),
    .out8(decoder_1_out8), .out9(decoder_1_out9), .out10(decoder_1_out10), .out11(decoder_1_out11),
    .out12(decoder_1_out12), .out13(decoder_1_out13), .out14(decoder_1_out14), .out15(decoder_1_out15),
    .sel(RegW), .en(reg_str));
  Pull_Resistor pull_resistor_1 (.node(RegW));
  or or_1 (or_1_out, psh, pll);
  Pull_Resistor pull_resistor_2 (.node({pull_resistor_2_node, MEMORY_ADDR}));
  Bit_Extender #(.out_width(3), .\type ("zero")) bit_extender_2 (.in(pull_resistor_2_node), .out(bit_extender_2_out));
  and and_1 (and_1_out, decoder_2_out1, we);
  or or_2 (or_2_out, we, mem_or_data);
  Multiplexer #(.width(32)) multiplexer_2 (
    .in0(addr), .in1(adder_1_out), .out({pull_resistor_2_node, MEMORY_ADDR}), .sel(or_2_out));
  Decoder #(.select(3)) decoder_2 (
    .out0(decoder_2_out0), .out1(decoder_2_out1), .out2(screenEN), .sel(bit_extender_2_out), .en(not_1_out));  // open: out3, out4, out5, out6, out7
  not not_1 (not_1_out, hlt);
  RAM #(.addrWidth(24), .dataWidth(32), .trigger("falling"), .\type ("nonvolatile")) ram_1 (
    .addr(MEMORY_ADDR), .we(and_1_out), .oe(1'b1), .clk(clock_1_out), .din(R1), .dout(ram_1_dout));
  Clock clock_1 (.out(clock_1_out));
  Multiplexer #(.width(32)) multiplexer_3 (.in0(multiplexer_1_out), .in1(stk_out), .out(multiplexer_3_out), .sel(pll));
  Clock clock_2 (.out(clock_2_out));
  Comparator #(.width(32)) comparator_1 (
    .a({pull_resistor_2_node, MEMORY_ADDR}), .b({32{1'b1}}), .eq(comparator_1_eq));  // open: gt, lt
  Multiplexer #(.width(32)) multiplexer_4 (
    .in0(multiplexer_3_out), .in1(ALU_out), .out(multiplexer_4_out), .sel(ALU_en));
  Register #(.width(32)) A (.D(multiplexer_4_out), .en(decoder_1_out0), .clk(clock_3_out), .Q(A_q));  // open: clr
  Clock clock_3 (.out(clock_3_out));
  Register #(.width(32)) I (.D(multiplexer_4_out), .en(decoder_1_out8), .clk(clock_3_out), .Q(I_q));  // open: clr
  Counter #(.trigger("falling")) counter_1 (
    .up(psh), .count(or_1_out), .clk(clock_2_out), .Q(counter_1_q));  // open: clr, load, D, carry
  Clock clock_4 (.out(clock_4_out));
  Keyboard keyboard_1 (.clk(clock_4_out), .re(comparator_1_eq), .data(keyboard_1_data));  // open: clr, avail
  assign bit_extender_3_out = {{16{1'b0}}, DATA};  // Bit_Extender bit_extender_3
  Multiplier #(.width(32)) multiplier_1 (
    .a(bit_extender_3_out), .b(32'h1000000), .out(multiplier_1_out));  // open: cin, cout
  assign MEMORY_OUT = decoder_2_out1 ? ram_1_dout : 32'bz;  // Controlled_Buffer controlled_buffer_1
  Register #(.width(32)) B (.D(multiplexer_4_out), .en(decoder_1_out1), .clk(clock_3_out), .Q(B_q));  // open: clr
  Register #(.width(32)) J (.D(multiplexer_4_out), .en(decoder_1_out9), .clk(clock_3_out), .Q(J_q));  // open: clr
  Adder #(.width(32)) adder_1 (.a(R2), .b(multiplier_1_out), .out(adder_1_out));  // open: cin, cout
  Register #(.width(32)) C (.D(multiplexer_4_out), .en(decoder_1_out2), .clk(clock_3_out), .Q(C_q));  // open: clr
  Register #(.width(32)) K (.D(multiplexer_4_out), .en(decoder_1_out10), .clk(clock_3_out), .Q(K_q));  // open: clr
  RAM #(.dataWidth(32)) ram_2 (
    .addr(counter_1_q), .we(psh), .oe(or_1_out), .clk(clock_2_out), .din(R1), .dout(stk_out));
  ROM #(.addrWidth(24), .dataWidth(32)) rom_1 (.addr(MEMORY_ADDR), .data(rom_1_data));
  Register #(.width(32)) D (.D(multiplexer_4_out), .en(decoder_1_out3), .clk(clock_3_out), .Q(D_q));  // open: clr
  Register #(.width(32)) L (.D(multiplexer_4_out), .en(decoder_1_out11), .clk(clock_3_out), .Q(L_q));  // open: clr
  assign bit_extender_4_out = {{25{1'b0}}, keyboard_1_data};  // Bit_Extender bit_extender_4
  assign MEMORY_OUT = comparator_1_eq ? bit_extender_4_out : 32'bz;  // Controlled_Buffer controlled_buffer_2
  Register #(.width(32)) E (.D(multiplexer_4_out), .en(decoder_1_out4), .clk(clock_3_out), .Q(E_q));  // open: clr
  Register #(.width(32)) M (.D(multiplexer_4_out), .en(decoder_1_out12), .clk(clock_3_out), .Q(M_q));  // open: clr
  assign MEMORY_OUT = decoder_2_out0 ? rom_1_data : 32'bz;  // Controlled_Buffer controlled_buffer_3
  Register #(.width(32)) F (.D(multiplexer_4_out), .en(decoder_1_out5), .clk(clock_3_out), .Q(F_q));  // open: clr
  Register #(.width(32)) N (.D(multiplexer_4_out), .en(decoder_1_out13), .clk(clock_3_out), .Q(N_q));  // open: clr
  Comparator #(.width(32)) comparator_2 (
    .a(R1), .b(R2), .gt(comparator_2_gt), .eq(comparator_2_eq), .lt(comparator_2_lt));
  Register #(.width(32)) G (.D(multiplexer_4_out), .en(decoder_1_out6), .clk(clock_3_out), .Q(G_q));  // open: clr
  Register #(.width(32)) O (.D(multiplexer_4_out), .en(decoder_1_out14), .clk(clock_3_out), .Q(O_q));  // open: clr
  or or_3 (or_3_out, comparator_2_gt, comparator_2_eq);
  or or_4 (or_4_out, comparator_2_lt, comparator_2_eq);
  D_Flip_Flop d_ff_1 (.D(d_ff_1_qn), .clk(clock_5_out), .Q(d_ff_1_q), .Qn(d_ff_1_qn));  // open: preset, reset
  Clock clock_5 (.out(clock_5_out));
  not not_2 (not_2_out, comparator_2_eq);
  Register #(.width(32)) H (.D(multiplexer_4_out), .en(decoder_1_out7), .clk(clock_3_out), .Q(H_q));  // open: clr
  Register #(.width(32)) P (.D(multiplexer_4_out), .en(decoder_1_out15), .clk(clock_3_out), .Q(P_q));  // open: clr
  and and_2 (and_2_out, multiplexer_5_out, jmp);
  Multiplexer #(.select(3)) multiplexer_5 (
    .in0(1'b1), .in1(comparator_2_eq), .in2(not_2_out), .in3(comparator_2_gt), .in4(comparator_2_lt),
    .in5(or_3_out), .in6(or_4_out), .out(multiplexer_5_out), .sel(DATA[2:0]));  // open: in7
  not not_3 (not_3_out, hlt);
  not not_4 (not_4_out, and_2_out);
  and and_3 (and_3_out, d_ff_1_q, not_4_out, not_5_out);
  not not_5 (not_5_out, hlt);
  Register #(.width(32)) inst_and_data (
    .D(MEMORY_OUT), .en(and_4_out), .clk(clock_6_out), .Q({DATA, RegW, RegR1, RegR2, inst_and_data_q}));  // open: clr
  Clock clock_6 (.out(clock_6_out));
  and and_4 (and_4_out, d_ff_1_qn, not_3_out);
  Counter #(.max('hffffffff), .width(32)) counter_2 (
    .load(and_2_out), .count(and_3_out), .clk(clock_7_out), .D(jmp_a), .Q(addr));  // open: clr, up, carry
  Clock clock_7 (.out(clock_7_out));
  Multiplexer #(.select(4), .width(32)) multiplexer_6 (
    .in0(A_q), .in1(B_q), .in2(C_q), .in3(D_q), .in4(E_q), .in5(F_q), .in6(G_q), .in7(H_q), .in8(I_q),
    .in9(J_q), .in10(K_q), .in11(L_q), .in12(M_q), .in13(N_q), .in14(O_q), .in15(P_q), .out(R1), .sel(RegR1));
  Multiplexer #(.select(4), .width(32)) multiplexer_7 (
    .in0(A_q), .in1(B_q), .in2(C_q), .in3(D_q), .in4(E_q), .in5(F_q), .in6(G_q), .in7(H_q), .in8(I_q),
    .in9(J_q), .in10(K_q), .in11(L_q), .in12(M_q), .in13(N_q), .in14(O_q), .in15(P_q), .out(R2), .sel(RegR2));
  Multiplexer #(.select(4), .width(32)) multiplexer_8 (
    .in0(A_q), .in1(B_q), .in2(C_q), .in3(D_q), .in4(E_q), .in5(F_q), .in6(G_q), .in7(H_q), .in8(I_q),
    .in9(J_q), .in10(K_q), .in11(L_q), .in12(M_q), .in13(N_q), .in14(O_q), .in15(P_q), .out(jmp_a),
    .sel(DATA[7:4]));
  Bit_Extender #(.in_width(32), .out_width(5)) bit_extender_5 (.in(R2), .out(bit_extender_5_out));
  Adder #(.width(32)) adder_2 (.a(R1), .b(R2), .out(adder_2_out));  // open: cin, cout
  Subtractor #(.width(32)) subtractor_1 (.a(R1), .b(R2), .out(subtractor_1_out));  // open: bin, bout
  Multiplier #(.width(32)) multiplier_2 (.a(R1), .b(R2), .out(multiplier_2_out));  // open: cin, cout
  Divider #(.width(32)) divider_1 (.a(R1), .b(R2), .out(divider_1_out));  // open: upper, rem
  Shifter #(.width(32)) shifter_1 (.in(R1), .\dist (bit_extender_5_out), .out(shifter_1_out));
  Shifter #(.shift("lr"), .width(32)) shifter_2 (.in(R1), .\dist (bit_extender_5_out), .out(shifter_2_out));
  ROM #(.addrWidth(4)) rom_2 (.addr(inst_and_data_q), .data(rom_2_data));
  Multiplexer #(.select(3), .width(32)) multiplexer_9 (
    .in0(adder_2_out), .in1(subtractor_1_out), .in2(multiplier_2_out), .in3(divider_1_out),
    .in4(shifter_1_out), .in5(shifter_2_out), .out(multiplexer_9_out), .sel(bit_extender_6_out));  // open: in6, in7
  Bit_Extender #(.in_width(16), .out_width(3)) bit_extender_6 (.in(DATA), .out(bit_extender_6_out));
  assign ALU_out = ALU_en ? multiplexer_9_out : 32'bz;  // Controlled_Buffer controlled_buffer_4
  assign {pll, psh, we, ALU_en, hlt, jmp, mem_or_data, reg_str} = d_ff_1_q ? rom_2_data : 8'bz;  // Controlled_Buffer controlled_buffer_5
  Pull_Resistor pull_resistor_3 (.node({pll, psh, we, ALU_en, hlt, jmp, mem_or_data, reg_str}));
  not not_6 (not_6_out, s_r_ff_1_q);
  Bit_Extender #(.in_width(24)) bit_extender_7 (.in(MEMORY_ADDR), .out(bit_extender_7_out));
  D_Flip_Flop d_ff_2 (.D(and_5_out), .clk(clock_8_out), .Q(d_ff_2_q));  // open: Qn, preset, reset
  and and_5 (and_5_out, comparator_3_gt, and_6_out);
  Clock clock_8 (.out(clock_8_out));
  and and_6 (and_6_out, we, not_6_out);
  or or_5 (or_5_out, d_ff_2_q, and_7_out);
  Comparator #(.mode("unsigned")) comparator_3 (
    .a(R1[31:24]), .b(8'h80), .gt(comparator_3_gt), .lt(comparator_3_lt));  // open: eq
  Register #(.trigger("high"), .width(7)) register_1 (
    .D(R1[30:24]), .en(and_6_out), .clk(clock_8_out), .Q(counter_3_q[12:6]));  // open: clr
  S_R_Flip_Flop s_r_ff_1 (
    .S(and_6_out), .R(or_5_out), .clk(clock_8_out), .Q(s_r_ff_1_q), .Qn(s_r_ff_1_qn));  // open: reset, preset
  Register #(.trigger("high")) register_2 (
    .D(bit_extender_7_out[7:0]), .en(and_6_out), .clk(clock_8_out), .Q(register_2_q), .clr(s_r_ff_1_qn));
  Register #(.trigger("high")) register_3 (
    .D(bit_extender_7_out[15:8]), .en(and_6_out), .clk(clock_8_out), .Q(register_3_q), .clr(s_r_ff_1_qn));
  Register #(.trigger("high"), .width(24)) register_4 (
    .D(R1[23:0]), .en(and_6_out), .clk(clock_8_out), .Q(register_4_q), .clr(s_r_ff_1_qn));
  and and_7 (and_7_out, counter_3_carry, counter_4_carry);
  // RGB_Video #(.cursor("No Cursor"), .height(256), .scale(8), .width(256)) rgb_video_1: pin names not known; wires that end beside it: clock_8_out, rgb_video_1_p2, rgb_video_1_p3, rgb_video_1_p4, rgb_video_1_p5
  and and_8 (rgb_video_1_p2, s_r_ff_1_q, pull_resistor_4_node);
  Counter #(.max('h7), .width(3)) counter_3 (
    .clr(s_r_ff_1_qn), .load(and_7_out), .count(s_r_ff_1_q), .clk(clock_8_out), .D(3'b000),
    .carry(counter_3_carry), .Q(counter_3_q[2:0]));  // open: up
  Counter #(.max('h7), .width(3)) counter_4 (
    .clr(s_r_ff_1_qn), .load(and_7_out), .count(counter_3_carry), .clk(clock_8_out), .D(3'b000),
    .carry(counter_4_carry), .Q(counter_3_q[5:3]));  // open: up
  ROM #(.addrWidth(13), .dataWidth(1)) rom_3 (.addr(counter_3_q));  // open: data
  Multiplexer #(.width(24)) multiplexer_10 (
    .in0({24{1'b0}}), .in1(register_4_q), .out(rgb_video_1_p5), .sel(pull_resistor_4_node));
  Pull_Resistor #(.pull(1)) pull_resistor_4 (.node(pull_resistor_4_node));
  Adder adder_3 (.a(register_2_q), .b(bit_extender_8_out), .out(rgb_video_1_p3));  // open: cin, cout
  assign bit_extender_8_out = {{5{1'b0}}, counter_3_q[2:0]};  // Bit_Extender bit_extender_8
  assign bit_extender_9_out = {{5{1'b0}}, counter_3_q[5:3]};  // Bit_Extender bit_extender_9
  Adder adder_4 (.a(register_3_q), .b(bit_extender_9_out), .out(rgb_video_1_p4));  // open: cin, cout
  assign pull_resistor_4_node = comparator_3_lt ? undriven : 1'bz;  // Controlled_Buffer controlled_buffer_6

  // Other names for the same wires on the sheet: jmp_addr[3:0] = DATA[7:4]

  // Notes on the sheet:
  //   contents of rom_1 (hex, n*v repeats v):
  //   bd002 d00005 0 0 1 1 20 10 20 ffffffff 16 2d002 d3 3d002 10d3 4d002 20d3 5d002 30d3 6d002 e0d3
  //   e20ff5 24 1134 7d002 f0d3 8d002 e0d3 e600f5 9d002 f0d3 222f4 ad002 e0d3 e10ff5 1
  //   contents of rom_2 (hex, n*v repeats v):
  //   0 8 1 3 11 4 20 40 81
  //   contents of rom_3 (hex, n*v repeats v):
  //   2123*0 1 1 6*0 1 1 6*0 1 1 6*0 1 1 14*0 1 1 21*0 1 0 0 1 4*0 1 0 0 1 52*0 1 0 0 1 0 0 0 6*1 0 0 0 1
  //   0 0 1 4*0 1 0 0 1 0 0 0 6*1 0 0 0 1 0 0 1 21*0 1 1 6*0 1 1 1 5*0 1 1 1 4*0 1 1 1 5*0 1 1 1 6*0 1 1
  //   20*0 1 1 0 0 0 1 0 0 1 1 0 0 1 6*0 1 6*0 1 6*0 1 0 0 1 1 0 0 1 0 0 0 1 1 26*0 1 1 0 0 1 1 10*0 1 1 0
  //   0 1 1 36*0 1 1 6*0 1 1 6*0 1 1 47*0 1 6*0 1 7*0 1 7*0 1 7*0 1 8*0 1 22*0 1 8*0 1 7*0 1 7*0 1 7*0 1
  //   6*0 1 23*0 1 6*0 1 1 1 6*0 1 47*0 1 1 6*0 1 1 4*0 6*1 0 0 6*1 4*0 1 1 6*0 1 1 46*0 1 1 6*0 1 1 5*0 1
  //   1 37*0 6*1 0 0 6*1 68*0 1 1 6*0 1 1 23*0 1 1 6*0 1 1 5*0 1 1 6*0 1 1 5*0 1 1 6*0 1 1 23*0 1 1 5*0 1
  //   0 0 1 4*0 1 0 1 1 4*0 1 1 0 1 4*0 1 0 0 1 5*0 1 1 23*0 1 6*0 1 1 7*0 1 7*0 1 7*0 1 6*0 1 1 1 21*0 1
  //   1 5*0 1 0 0 1 7*0 1 6*0 1 6*0 1 6*0 4*1 21*0 1 1 5*0 1 0 0 1 6*0 1 5*0 1 0 0 1 5*0 1 1 32*0 1 6*0 1
  //   1 5*0 1 0 1 4*0 1 0 0 1 4*0 5*1 6*0 1 20*0 4*1 4*0 1 7*0 1 1 1 8*0 1 4*0 1 0 0 1 5*0 1 1 22*0 1 1
  //   5*0 1 7*0 1 1 1 5*0 1 0 0 1 4*0 1 0 0 1 5*0 1 1 21*0 4*1 6*0 1 6*0 1 7*0 1 6*0 1 7*0 1 24*0 1 1 5*0
  //   1 0 0 1 5*0 1 1 5*0 1 0 0 1 4*0 1 0 0 1 5*0 1 1 22*0 1 1 5*0 1 0 0 1 4*0 1 0 0 1 5*0 1 1 1 7*0 1 5*0
  //   1 1 22*0 1 1 6*0 1 1 22*0 1 1 6*0 1 1 22*0 1 1 6*0 1 1 14*0 1 1 6*0 1 1 5*0 1 1 25*0 1 1 4*0 1 1 4*0
  //   1 1 6*0 1 1 8*0 1 1 8*0 1 1 34*0 6*1 10*0 6*1 26*0 1 1 8*0 1 1 8*0 1 1 6*0 1 1 4*0 1 1 4*0 1 1 24*0
  //   1 1 5*0 1 0 0 1 7*0 1 6*0 1 15*0 1 21*0 4*1 0 0 0 1 4*0 1 0 0 1 0 1 1 0 1 0 0 1 0 1 1 0 1 0 0 1 0 0
  //   0 1 1 0 0 0 1 1 23*0 1 1 5*0 1 0 0 1 4*0 1 0 0 1 4*0 1 0 0 1 4*0 4*1 4*0 1 0 0 1 20*0 1 1 1 5*0 1 0
  //   0 1 4*0 1 0 0 1 4*0 1 1 1 5*0 1 0 0 1 4*0 1 1 1 22*0 1 1 5*0 1 0 0 1 4*0 1 7*0 1 7*0 1 0 0 1 5*0 1 1
  //   21*0 1 1 1 5*0 1 0 0 1 4*0 1 0 0 1 4*0 1 0 0 1 4*0 1 0 0 1 4*0 1 1 1 21*0 4*1 4*0 1 7*0 1 1 1 5*0 1
  //   7*0 1 7*0 4*1 20*0 4*1 4*0 1 7*0 1 1 1 5*0 1 7*0 1 7*0 1 24*0 1 1 5*0 1 0 0 1 4*0 1 7*0 1 0 1 1 4*0
  //   1 0 0 1 5*0 1 1 21*0 1 0 0 1 4*0 1 0 0 1 4*0 1 0 0 1 4*0 4*1 4*0 1 0 0 1 4*0 1 0 0 1 19*0 5*1 5*0 1
  //   7*0 1 7*0 1 7*0 1 5*0 5*1 22*0 1 1 7*0 1 7*0 1 7*0 1 4*0 1 0 0 1 5*0 1 1 21*0 1 0 0 1 4*0 1 0 1 5*0
  //   1 1 6*0 1 1 6*0 1 0 1 5*0 1 0 0 1 20*0 1 7*0 1 7*0 1 7*0 1 7*0 1 7*0 4*1 19*0 1 4*0 1 0 0 1 1 0 0 1
  //   1 0 0 1 0 1 1 0 1 0 0 1 4*0 1 0 0 1 4*0 1 0 0 1 4*0 1 19*0 1 0 0 1 4*0 1 1 0 1 4*0 1 1 0 1 4*0 1 0 1
  //   1 4*0 1 0 1 1 4*0 1 0 0 1 20*0 4*1 0 0 0 1 4*0 1 0 0 1 4*0 1 0 0 1 4*0 1 0 0 1 4*0 1 0 0 0 4*1 20*0
  //   1 1 1 5*0 1 0 0 1 4*0 1 0 0 1 4*0 1 1 1 5*0 1 7*0 1 23*0 1 1 1 4*0 1 0 0 0 1 0 0 0 1 0 0 0 1 0 0 0 1
  //   0 0 1 1 4*0 4*1 8*0 1 19*0 1 1 1 5*0 1 0 0 1 4*0 1 0 0 1 4*0 1 1 1 5*0 1 0 1 5*0 1 0 0 1 21*0 1 1
  //   5*0 1 8*0 1 1 8*0 1 4*0 1 0 0 1 5*0 1 1 20*0 5*1 5*0 1 7*0 1 7*0 1 7*0 1 7*0 1 22*0 1 0 0 1 4*0 1 0
  //   0 1 4*0 1 0 0 1 4*0 1 0 0 1 4*0 1 0 0 1 5*0 1 1 20*0 1 4*0 1 0 0 1 4*0 1 0 0 1 4*0 1 0 0 0 1 0 0 1
  //   4*0 1 0 0 1 5*0 1 1 20*0 1 4*0 1 0 0 1 4*0 1 0 0 1 4*0 1 0 0 1 0 1 1 0 1 0 0 1 0 1 1 0 1 0 0 0 1 0 0
  //   1 19*0 1 4*0 1 0 0 0 1 0 0 1 5*0 1 1 6*0 1 1 5*0 1 0 0 1 0 0 0 1 4*0 1 18*0 1 0 0 0 1 4*0 1 0 1 6*0
  //   1 7*0 1 7*0 1 7*0 1 21*0 5*1 6*0 1 6*0 1 6*0 1 6*0 1 7*0 5*1 20*0 1 1 1 5*0 1 7*0 1 7*0 1 7*0 1 7*0
  //   1 1 1 22*0 1 7*0 1 8*0 1 7*0 1 8*0 1 7*0 1 21*0 1 1 1 7*0 1 7*0 1 7*0 1 7*0 1 5*0 1 1 1 21*0 1 1 5*0
  //   1 0 0 1 0 0 0 1 4*0 1 82*0 6*1 19*0 1 1 7*0 1 1 70*0 1 1 5*0 1 0 0 1 4*0 1 0 0 1 5*0 1 1 0 1 19*0 1
  //   7*0 1 7*0 1 1 1 5*0 1 0 0 1 4*0 1 0 0 1 5*0 1 1 38*0 1 1 5*0 1 7*0 1 8*0 1 1 24*0 1 7*0 1 5*0 1 1 1
  //   4*0 1 0 0 1 4*0 1 0 0 1 5*0 1 1 22*0 1 1 5*0 1 0 0 1 4*0 4*1 4*0 1 7*0 1 0 0 1 5*0 1 1 22*0 1 1 5*0
  //   1 0 0 1 4*0 1 6*0 1 1 1 6*0 1 7*0 1 24*0 1 1 5*0 1 0 0 1 5*0 1 1 1 7*0 1 4*0 1 0 0 1 5*0 1 1 21*0 1
  //   7*0 1 7*0 1 1 1 5*0 1 0 0 1 4*0 1 0 0 1 4*0 1 0 0 1 22*0 1 14*0 1 1 7*0 1 7*0 1 6*0 1 1 1 22*0 1
  //   15*0 1 7*0 1 4*0 1 0 0 1 5*0 1 1 22*0 1 7*0 1 7*0 1 0 1 5*0 1 1 6*0 1 1 6*0 1 0 1 21*0 1 7*0 1 7*0 1
  //   7*0 1 7*0 1 8*0 1 38*0 1 0 1 4*0 1 0 1 0 1 0 0 0 1 0 1 0 1 0 0 0 1 0 0 0 1 45*0 1 1 6*0 1 0 1 5*0 1
  //   0 1 37*0 1 1 5*0 1 0 0 1 4*0 1 0 0 1 5*0 1 1 22*0 1 1 5*0 1 0 0 1 4*0 1 0 0 1 4*0 1 1 1 5*0 1 7*0 1
  //   24*0 1 1 5*0 1 0 0 1 4*0 1 0 0 1 5*0 1 1 1 7*0 1 7*0 1 1 44*0 1 1 5*0 1 7*0 1 32*0 1 1 1 4*0 1 8*0 1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
endmodule
